# Fritzing sketch Untitled Sketch 2 (saved by Fritzing 0.8.0b)
breadboards: 1

parts:
  Part1 = Arduino Pro Mini v13
  U1 = microSD Socket [package="Molex 502774-0891 [SMD]"]
  Adafruit_Bluefruit_HID1 = Adafruit Bluefruit Bluetooth Module
  GPS1 = Adafruit Ultimate GPS Breakout
  BATT1 = LiPoly Battery (1300mAh)  # not connected

nets:
  GND: Part1.GND, U1.GND, Adafruit_Bluefruit_HID1.Ground, GPS1.GND
  VCC: Part1.VCC, U1.VCC, Adafruit_Bluefruit_HID1.3v, Adafruit_Bluefruit_HID1.G, GPS1.VIN
  N1: Part1.D13/SCK, U1.SCK
  N2: Part1.D12/MISO, U1.DI
  N3: Part1.D11_PWM/MOSI, U1.DO
  N4: Part1.D4, U1.CS
  N5: Part1.D3_PWM, GPS1.TX
  N6: Part1.D2, GPS1.RX
  N7: Part1.D1/RX, Adafruit_Bluefruit_HID1.TX
  N8: Part1.D0/TX, Adafruit_Bluefruit_HID1.RX, Adafruit_Bluefruit_HID1.L1

custom parts:
  LiPoly Battery (1300mAh): Lithium Ion Polymer Battery (1300mAh)
