# Fritzing sketch footie (saved by Fritzing 0.8.0b)
breadboards: 1

parts:
  U1 = microSD Socket [package="Molex 502774-0891 [SMD]"]
  Adafruit_Bluefruit_HID1 = Adafruit Bluefruit Bluetooth Module
  GPS1 = Adafruit Ultimate GPS Breakout
  BATT1 = LiPoly Battery (1300mAh)  # not connected
  S1 = Pushbutton [package="[SMD]"]
  S2 = Pushbutton [package="[SMD]"]
  LED1 = RGB LED (com. cathode, rgb) [package="5 mm [THT]"]
  U2 = Voltage Regulator - 3.3V [package="TO220 [THT]"]
  Part1 = Arduino Pro Mini v13
  Q1 = NPN-Transistor [package="TO92 [THT]"]

nets:
  D4: U1.CS, Part1.D4
  MISO: U1.DI, Part1.D12/MISO
  3.3V: U1.VCC, Adafruit_Bluefruit_HID1.3v, Adafruit_Bluefruit_HID1.G, GPS1.VIN, U2.output_voltage
  SCK: U1.SCK, Part1.D13/SCK
  GND: U1.GND, GPS1.GND, S1.Pin_1, S1.Pin_2, S2.Pin_1, S2.Pin_2, LED1.common_cathode, U2.GND, Part1.GND, Q1.C
  MOSI: U1.DO, Part1.D11_PWM/MOSI
  N1: Adafruit_Bluefruit_HID1.TX, Part1.D1/RX
  N2: Adafruit_Bluefruit_HID1.RX, Adafruit_Bluefruit_HID1.L1, Part1.D0/TX
  N3: Adafruit_Bluefruit_HID1.Ground, Q1.E
  D8: GPS1.TX, Part1.D8
  D7: GPS1.RX, Part1.D7
  N4: S1.Pin_3, S1.Pin_4, Part1.D3_PWM
  N5: S2.Pin_3, S2.Pin_4, Part1.D2
  N6: LED1.red_anode, Part1.D10_PWM/SS
  N7: LED1.green_anode, Part1.D6_PWM
  N8: LED1.blue_anode, Part1.D9_PWM
  N9: U2.input_voltage, Part1.VCC
  N10: Part1.D5_PWM, Q1.B

custom parts:
  LiPoly Battery (1300mAh): Lithium Ion Polymer Battery (1300mAh)
